# Fritzing sketch BAC_05_Capacitive_Touch (saved by Fritzing 0.9.3b)
breadboards: 1

parts:
  Part1 = Arduino Uno (Rev3) - ICSP
  LED1 = smd LED [color="Red (633nm)" package="0603 [SMD]"]
  CAPSENSE1 = AT42QT1010 Momentary Capsense Breakout

nets:
  N1: Part1.D13/SCK, LED1.anode
  GND: Part1.GND, LED1.cathode, CAPSENSE1.GND
  N2: Part1.D2, CAPSENSE1.OUT
  5V: Part1.5V, CAPSENSE1.VDD

custom parts:
  AT42QT1010 Momentary Capsense Breakout: A capacitive touch momentary switch breakout for the AT42QT1010 chip.
