# Fritzing sketch BAC_10_LED (saved by Fritzing 0.9.3b)

parts:
  Part1 = Arduino Uno (Rev3) - ICSP
  LED1 = smd LED [color="Red (633nm)" package="0603 [SMD]"]

nets:
  N1: Part1.D11_PWM/MOSI, LED1.anode
  N2: Part1.GND, LED1.cathode
