# Fritzing sketch BAC_14_Relay_Power (saved by Fritzing 0.9.3b)

parts:
  Part1 = Arduino Uno (Rev3) - ICSP
  KY-1 = Keyes Relay [package=THT]
  LED1 = LEDs [package=led10mm]
  BAT1 = BC9VPC [package=bc9vpc]

nets:
  N1: Part1.D13/SCK, KY-1.signal
  N2: Part1.5V, KY-1.power
  N3: Part1.GND, KY-1.ground
  N4: KY-1.C, BAT1.V+
  N5: KY-1.NO, LED1.A
  N6: LED1.C, BAT1.V-

notes:
  12v LED strip!

custom parts:
  Keyes Relay: The Keyes 5V relay module is suitable for SCM development, home appliance control. It uses a 5V~12V TIL control signal which can control DC / AC signal.
