# Fritzing sketch BAC_16_MOSFET (saved by Fritzing 0.9.3b)
breadboards: 1

parts:
  Part2 = Arduino Uno (Rev3) - ICSP
  LED2 = LEDs [package=led10mm]  # not connected
  BAT2 = BC9VPC [package=bc9vpc]

nets:
  N1: Part2.GND, BAT2.V-

notes:
  INPUT OUTPUT
  C
  - -
  + +
  MOSFET PWR BOARD
